# Fritzing sketch Clock_Body_REV_A (saved by Fritzing 0.9.3b)
circuit board: 8.46667cm x 5.64444cm
breadboards: 1

parts:
  Part2 = Arduino Nano (Rev3.0) (ICSP)
  TP1 = TP4056 [chip_label=TP4056 package="DIP (Dual Inline) [THT]"]
  T1 = TMP36 Temperature Sensor [package="TO92 [THT]"]
  J1 = male pin header, 7 pins [form="♂ (male)"]
  ZS-042_RTC1 = ZS-042 RTC Module
  JP1 = Header 2 [package=jst-2-pth-ns]
  J2 = female pin header, 4 pins [form="♀ (female)"]
  J3 = female pin header, 4 pins [form="♀ (female)"]

nets:
  GND: Part2.GND, T1.GND, J1.pin7, ZS-042_RTC1.GND#0, J2.pin4, J3.pin1
  N1: Part2.D5, J2.pin1
  N2: Part2.D6, J2.pin2
  N3: Part2.D7, J2.pin3
  N4: Part2.D8, J1.pin2
  N5: Part2.D9, J1.pin3
  N6: Part2.D10, J1.pin1
  N7: Part2.D12/MISO, J3.pin2
  5V: Part2.5V, J1.pin6, ZS-042_RTC1.VCC
  N8: Part2.A0, T1.Vout
  N9: Part2.3V3, T1.+Vs
  N10: Part2.D13/SCK, J1.pin5, ZS-042_RTC1.SCL
  N11: Part2.D11/MOSI, J1.pin4, ZS-042_RTC1.SDA
  N12: TP1.pin4, JP1.2
  N13: TP1.pin5, JP1.1

notes:
  + to Boost
  - to Boost
  - F/Boost to Nano
  + F/Boost to Nano

custom parts:
  TP4056: A DIP stand-in part for whatever IC you want. With 6 pins on a 300mil dual inline package (DIP) footprint.
