# Fritzing sketch Clock_Top_REV_A (saved by Fritzing 0.9.3b)
circuit board: 8.46667cm x 2.37691cm
breadboards: 1

parts:
  J6 = male pin header, 4 pins [form="♂ (male)"]
  S3 = Pushbutton [package="[THT]"]
  J7 = Piezo Speaker
  S2 = Pushbutton [package="[THT]"]
  S1 = Pushbutton [package="[THT]"]
  J4 = male pin header, 4 pins [form="♂ (male)"]

nets:
  N1: J6.pin1, J7.pin1
  N2: J6.pin2, J7.pin2
  N3: S3.Pin_1, S3.Pin_2, S2.Pin_1, S2.Pin_2, S1.Pin_1, S1.Pin_2, J4.pin4
  N4: S3.Pin_3, J4.pin3
  N5: S2.Pin_3, S2.Pin_4, J4.pin2
  N6: S1.Pin_3, S1.Pin_4, J4.pin1
